# Fritzing sketch a4988 (saved by Fritzing 0.9.3b)
breadboards: 1

parts:
  MCU3 = Raspberry Pi Zero
  Pololu_A1 = Pololu A4988 [package=SO16]
  JACK1 = 2.1mm Barrel Jack with Terminal Block
  M1 = Stepper Motor - Bipolar

nets:
  N1: MCU3.pin_1, Pololu_A1.VDD
  N2: MCU3.pin_6, MCU3.pin_34, Pololu_A1.GND, JACK1.NEG
  N3: MCU3.pin_35, Pololu_A1.DIR
  N4: MCU3.pin_37, MCU3.pin_40, Pololu_A1.STEP
  N5: Pololu_A1.RESET, Pololu_A1.SLEEP
  N6: Pololu_A1.1B, M1.D
  N7: Pololu_A1.1A, M1.B
  N8: Pololu_A1.2A, M1.C
  N9: Pololu_A1.2B, M1.A
  N10: Pololu_A1.VMOT, JACK1.POS

notes:
  コイル1
  コイル2
  モーター用DC電源(モータスペックに依る）
  A4988
  ２相　バイポーラ　ステッピングモータ
  RESET
  SLEEP
  STEP
  DIR
  VMOT
  MOTOR GND
  LOGIC GND
  VDD
