# Fritzing sketch ads1015_zero (saved by Fritzing 0.9.3b)
breadboards: 1

parts:
  パーツ1 = Adafruit ADS1115 16Bit I2C ADC [part_number="Adafruit #1085"]
  MCU1 = Raspberry Pi Zero
  C1 = Capacitor [part_number=1μF package=cap-pth-large]
  R1 = Rotary Potentiometer (Small) [maximum_resistance=10kΩ package=THT]

nets:
  N1: パーツ1.AIN0, C1.1, R1.wiper
  N2: パーツ1.ADDR, パーツ1.GND, MCU1.pin_6, MCU1.pin_34, C1.2, R1.leg1
  N3: パーツ1.SDA, MCU1.pin_3
  N4: パーツ1.SCL, MCU1.pin_5
  N5: パーツ1.VDD, MCU1.pin_1, MCU1.pin_17, R1.leg2

custom parts:
  Adafruit ADS1115 16Bit I2C ADC: For microcontrollers without an analog-to-digital converter or when you want a higher-precision ADC, the ADS1115 provides 16-bit precision at 860 samples/second over I2C. The chip can be configured as 4 single-ended input channels, or two differential channels. As a nice bonus, it even includes a programmable gain amplifier, up to x16, to help boost up smaller single/differential signals to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
  Raspberry Pi Zero: The Raspberry Pi Zero is half the size of a Model A+, with twice the utility. A tiny Raspberry Pi that’s affordable enough for any project! · 1Ghz, Single-core CPU · 512MB RAM · Mini HDMI and USB On-The-Go ports · Micro USB power · HAT-compatible 40-pin header. Jan 2018: In this version schematic has been changed so the pins match the GPIO connector. I.e. the left hand pins are all the pins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
