# Fritzing sketch ADS1115_LoadCell_zero (saved by Fritzing 0.9.3b)

parts:
  パーツ1 = Adafruit ADS1115 16Bit I2C ADC [part_number="Adafruit #1085"]
  LoadCell = Load Cell [chip_label=LoadCell package="SIP (Single Inline) [THT]"]
  MCU1 = Raspberry Pi Zero

nets:
  N1: パーツ1.AIN1, LoadCell.pin2
  N2: パーツ1.AIN0, LoadCell.pin1
  N3: パーツ1.SDA, MCU1.pin_3
  N4: パーツ1.SCL, MCU1.pin_5
  N5: パーツ1.GND, LoadCell.pin3, MCU1.pin_6, MCU1.pin_39
  N6: パーツ1.VDD, MCU1.pin_1, MCU1.pin_17
  N7: LoadCell.pin4, MCU1.pin_2, MCU1.pin_4

custom parts:
  Adafruit ADS1115 16Bit I2C ADC: For microcontrollers without an analog-to-digital converter or when you want a higher-precision ADC, the ADS1115 provides 16-bit precision at 860 samples/second over I2C. The chip can be configured as 4 single-ended input channels, or two differential channels. As a nice bonus, it even includes a programmable gain amplifier, up to x16, to help boost up smaller single/differential signals to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
  Load Cell: A SIP stand-in part for whatever you want. With 4 pins on a 300 mil single inline package (SIP) footprint.
  Raspberry Pi Zero: The Raspberry Pi Zero is half the size of a Model A+, with twice the utility. A tiny Raspberry Pi that’s affordable enough for any project! · 1Ghz, Single-core CPU · 512MB RAM · Mini HDMI and USB On-The-Go ports · Micro USB power · HAT-compatible 40-pin header. Jan 2018: In this version schematic has been changed so the pins match the GPIO connector. I.e. the left hand pins are all the pins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
