# Fritzing sketch PiZero_ADT7410 (saved by Fritzing 0.9.3b)
breadboards: 1

parts:
  MCU1 = Raspberry Pi Zero
  U1 = ADT7410 AKIZUKI [package="SIP (Single Inline) [THT]"]

nets:
  N1: MCU1.pin_1, U1.pin4
  N2: MCU1.pin_3, U1.pin2
  N3: MCU1.pin_5, U1.pin3
  N4: MCU1.pin_6, MCU1.pin_9, U1.pin1

custom parts:
  ADT7410 AKIZUKI: ADT7410 I2C breakout AKIZUKI ver
