# Fritzing sketch AS5600 (saved by Fritzing 0.9.3b)

parts:
  MCU1 = Raspberry Pi Zero
  A1 = AS5600 module

nets:
  N1: MCU1.pin_1, A1.Pin_1
  N2: MCU1.pin_3, A1.Pin_5
  N3: MCU1.pin_5, A1.Pin_6
  N4: MCU1.pin_6, A1.Pin_3

custom parts:
  AS5600 module: .This module is mainly placed behind the stepper motor to obtain the rotation angle of the stepper motor.
