# Fritzing sketch ENS160 (saved by Fritzing 0.9.3b)
breadboards: 1

parts:
  MCU2 = Raspberry Pi Zero
  A2 = ENS160 AHT21

nets:
  N1: MCU2.pin_1, MCU2.pin_17, A2.Pin_2
  N2: MCU2.pin_3, A2.Pin_5
  N3: MCU2.pin_5, A2.Pin_4
  N4: MCU2.pin_6, MCU2.pin_25, A2.Pin_3

custom parts:
  ENS160 AHT21: The CO2 Gas- Air- Sensor is based on ENS160 in combination with an AHT21 Temperature Humidity Sensor.
