# Fritzing sketch PiZero_gpio-camera (saved by Fritzing 0.9.3b)
breadboards: 1

parts:
  S1 = Pushbutton [package=THT]
  U1 = TCM8240MD [package=tcm8240md]
  U2 = IC, SIP package, 5 pins [chip_label=piCamera]
  MCU1 = Raspberry Pi Zero

nets:
  N1: S1.leg0, MCU1.pin_29
  N2: S1.leg1, MCU1.pin_25, MCU1.pin_34
  N3: U1.GND, U2.pin2, U2.pin5
  N4: U1.IOVDD, U2.pin4
  N5: U1.DCLK, U2.pin3
  N6: U1.DOUT7, U2.pin1

notes:
  Raspberry Pi カメラ
  専用コネクタに専用ケーブルで接続する

custom parts:
  Pushbutton: A generic pushbutton.
