# Fritzing sketch PiZero_gpio-inout (saved by Fritzing 0.9.3b)
breadboards: 1

parts:
  MCU1 = Raspberry Pi Zero
  S1 = Pushbutton [package=THT]
  LED2 = LED - 5mm [color="Red (633nm)" package="5 mm [THT]"]
  R3 = Resistor [tolerance=±5% resistance=1k part_number="茶黒赤金　　" package="2512 [SMD]"]

nets:
  N1: MCU1.pin_25, MCU1.pin_34, S1.leg0, LED2.cathode
  N2: MCU1.pin_29, S1.leg1
  N3: MCU1.pin_37, R3.Pin_1
  N4: LED2.anode, R3.Pin_0

custom parts:
  Pushbutton: A generic pushbutton.
