# Fritzing sketch GroveWaterLevelSensor (saved by Fritzing 0.9.5d)

parts:
  Raspberry_Pi_1 = Raspberry Pi 3 [part_number=RPI-3-V1.2]
  Grove1 = Grove Water Level Sensor

nets:
  3V3: Raspberry_Pi_1.3v3, Grove1.VCC
  N1: Raspberry_Pi_1.GPIO2, Grove1.SDA
  N2: Raspberry_Pi_1.GPIO3, Grove1.SCL
  GND: Raspberry_Pi_1.GND, Grove1.GND
