# Fritzing sketch PiZero_gpio0MotorC (saved by Fritzing 0.9.3b)

parts:
  JACK1 = 2.1mm Barrel Jack with Terminal Block
  MCU1 = Raspberry Pi Zero
  M1 = CHIBI Geared Motor [package="SIP (Single Inline) [THT]"]
  M2 = hcmmodu0083 [package=THT]

nets:
  N1: JACK1.POS, M2.pin5
  N2: JACK1.NEG, M2.pin4
  N3: MCU1.pin_6, MCU1.pin_34, M2.pin3
  N4: MCU1.pin_37, M2.pin1
  N5: M1.pin1, M2.pin7
  N6: M1.pin2, M2.pin6

notes:
  DC 5V MOTOR POWER
  -
  +

custom parts:
  CHIBI Geared Motor: Micro Geared Motor
  hcmmodu0083: hcmmodu0083 IRF540 Mosfet driver module
