# Fritzing sketch PiZero_gpio0MotorD_2 (saved by Fritzing 0.9.3b)

parts:
  JACK1 = 2.1mm Barrel Jack with Terminal Block
  MCU1 = Raspberry Pi Zero
  ギヤードモータ = GearedMotor [package=Motor]
  MOSFET1 = D4184 MOSFET Module [chip_label=IC package="SIP (Single Inline) [THT]"]

nets:
  N1: JACK1.POS, MOSFET1.VIN+
  N2: JACK1.NEG, MOSFET1.VIN-
  N3: MCU1.pin_9, MCU1.pin_34, MOSFET1.GND
  N4: MCU1.pin_37, MOSFET1.TRIG
  N5: ギヤードモータ.pin1, MOSFET1.OUT-
  N6: ギヤードモータ.pin2, MOSFET1.OUT+

notes:
  DC 5V MOTOR POWER
  -
  +

custom parts:
  GearedMotor: Micro Geared Motor
  D4184 MOSFET Module: Generic D4184 Dual MOSFET Module
