# Fritzing sketch ISD1820 sketch (saved by Fritzing 0.9.3b)

parts:
  MCU1 = Raspberry Pi Zero
  U3 = ISD1820 [chip_label=ISD1820 package="SIP (Single Inline) [THT]"]
  SP1 = SPEAKER [package=pcb_mount_speaker]

nets:
  N1: MCU1.pin_2, MCU1.pin_4, U3.VCC
  N2: MCU1.pin_6, MCU1.pin_39, U3.GND
  N3: MCU1.pin_37, U3.P-L
  N4: U3.FT1, U3.NC#8
  N5: U3.NC#9, U3.P-E0
  N6: U3.SP0, SP1.+
  N7: U3.SP1, SP1.-

custom parts:
  ISD1820: Vioce recoder module ISD1820
