# Fritzing sketch MPU9250_zero (saved by Fritzing 0.9.3b)

parts:
  MPU9250_MPU-1 = SparkFun IMU Breakout - MPU-9250 [part_number=" SEN-13762"]
  MCU1 = Raspberry Pi Zero

nets:
  N1: MPU9250_MPU-1.SCL/SCLK, MCU1.pin_5
  N2: MPU9250_MPU-1.SDA/SDI, MCU1.pin_3
  N3: MPU9250_MPU-1.VDD, MCU1.pin_1
  N4: MPU9250_MPU-1.GND, MCU1.pin_6, MCU1.pin_9

notes:
  GND
  3.3V
  SDA
  SCL

custom parts:
  SparkFun IMU Breakout - MPU-9250: The SparkFun MPU-9250 IMU Breakout features the latest 9-axis MEMS sensor from InvenSense. Each of these 9DoF breakouts feature an MPU-9250 with a System in Package (SiP) that combines two chips: the MPU-6500, which contains a 3-axis gyroscope as well as a 3-axis accelerometer, and the AK8963, which features a 3-axis magnetometer. This breakout has been designed to be smaller than some of our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
  Raspberry Pi Zero: The Raspberry Pi Zero is half the size of a Model A+, with twice the utility. A tiny Raspberry Pi that’s affordable enough for any project! · 1Ghz, Single-core CPU · 512MB RAM · Mini HDMI and USB On-The-Go ports · Micro USB power · HAT-compatible 40-pin header. Jan 2018: In this version schematic has been changed so the pins match the GPIO connector. I.e. the left hand pins are all the pins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
