# Fritzing sketch PCF8591_zero (saved by Fritzing 0.9.3b)

parts:
  U2 = PCF8591 AD DA sensor board [chip_label=IC package="SIP (Single Inline) [THT]"]
  MCU1 = Raspberry Pi Zero

nets:
  N1: U2.SDA, MCU1.pin_3
  N2: U2.SCL, MCU1.pin_5
  N3: U2.VCC, MCU1.pin_1, MCU1.pin_17
  N4: U2.GND, MCU1.pin_6, MCU1.pin_30
  N5: U2.AOUT, U2.AIN3
  N6: U2.AIN2, U2.INPUT2
  N7: U2.AIN1, U2.INPUT1
  N8: U2.AIN0, U2.INPUT0

custom parts:
  PCF8591 AD DA sensor board: PCA8591 AD DA sensor board
  Raspberry Pi Zero: The Raspberry Pi Zero is half the size of a Model A+, with twice the utility. A tiny Raspberry Pi that’s affordable enough for any project! · 1Ghz, Single-core CPU · 512MB RAM · Mini HDMI and USB On-The-Go ports · Micro USB power · HAT-compatible 40-pin header. Jan 2018: In this version schematic has been changed so the pins match the GPIO connector. I.e. the left hand pins are all the pins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
