# Fritzing sketch raspi3_qr-scanner (saved by Fritzing 0.9.5d)

parts:
  Raspberry_Pi_1 = Raspberry Pi 3 [part_number=RPI-3-V1.2]
  QR1 = QR_scanner

nets:
  N1: Raspberry_Pi_1.GPIO2, QR1.SDA
  N2: Raspberry_Pi_1.GPIO3, QR1.SCL
  GND: Raspberry_Pi_1.GND, QR1.GND
  5V: Raspberry_Pi_1.5V, QR1.VCC

custom parts:
  QR_scanner: A QR code scanner that supports both 1D and 2D symbologies. The side switch selects I²C or UART; it includes a trigger button and a red aiming LED.
