# Fritzing sketch PiZero_remote_camera (saved by Fritzing 0.9.3b)

parts:
  U1 = TCM8240MD [package=tcm8240md]
  U2 = IC, SIP package, 5 pins [chip_label=piCamera]
  MCU1 = Raspberry Pi Zero  # not connected

nets:
  N1: U1.GND, U2.pin2, U2.pin5
  N2: U1.IOVDD, U2.pin4
  N3: U1.DCLK, U2.pin3
  N4: U1.DOUT7, U2.pin1

notes:
  Raspberry Pi カメラ
  専用コネクタに専用ケーブルで接続する
