# Fritzing sketch SHT30_gpioin (saved by Fritzing 0.9.3b)
breadboards: 1

parts:
  U2 = SHT30 breakout [package="SIP (Single Inline) [THT]"]
  MCU2 = Raspberry Pi Zero
  S2 = Pushbutton [package=THT]

nets:
  N1: U2.pin1, MCU2.pin_1
  N2: U2.pin2, MCU2.pin_6, MCU2.pin_9, MCU2.pin_25, MCU2.pin_34, S2.leg1
  N3: U2.pin3, MCU2.pin_5
  N4: U2.pin4, MCU2.pin_3
  N5: MCU2.pin_29, S2.leg0

custom parts:
  SHT30 breakout: SHT30 Temperature Humidity sensor
  Pushbutton: A generic pushbutton.
