# Fritzing sketch SCD40 (saved by Fritzing 0.9.3b)
breadboards: 1

parts:
  MCU1 = Raspberry Pi Zero
  U3 = SIP - 4 pins [chip_label=IC package="SIP (Single Inline) [THT]"]

nets:
  N1: MCU1.pin_1, MCU1.pin_17, U3.pin2
  N2: MCU1.pin_3, U3.pin4
  N3: MCU1.pin_5, U3.pin3
  N4: MCU1.pin_6, MCU1.pin_20, U3.pin1

custom parts:
  SIP - 4 pins: A SIP stand-in part for whatever you want. With 4 pins on a 300 mil single inline package (SIP) footprint.
