# Fritzing sketch GY-NEO6MV2 (saved by Fritzing 0.9.3b)

parts:
  M1 = NEO-6M GPS Module [part_number=GY-GPS6MV2]
  MCU1 = Raspberry Pi Zero

nets:
  N1: M1.GND, MCU1.pin_6, MCU1.pin_34
  N2: M1.Tx, MCU1.pin_10
  N3: M1.Vcc, MCU1.pin_2, MCU1.pin_4

custom parts:
  NEO-6M GPS Module: GY-GPS6MV2 NEO-6M GPS Module Module based on U-blox NEO-6M GPS engine, incorporating regulator for 3.3-5V DC input, MS621FE-compatible rechargeable battery for backup and EEPROM for storing configuration settings. Links: NEO-6 series product information page NEO-6 Datasheet
