# Fritzing sketch SHT30 (saved by Fritzing 0.9.3b)
breadboards: 1

parts:
  U2 = SHT30 breakout [package="SIP (Single Inline) [THT]"]
  MCU2 = Raspberry Pi Zero

nets:
  N1: U2.pin1, MCU2.pin_1
  N2: U2.pin2, MCU2.pin_6, MCU2.pin_9
  N3: U2.pin3, MCU2.pin_5
  N4: U2.pin4, MCU2.pin_3

custom parts:
  SHT30 breakout: SHT30 Temperature Humidity sensor
