# Fritzing sketch SSD1308_zero (saved by Fritzing 0.9.3b)

parts:
  MCU1 = Raspberry Pi Zero
  Grove1 = Grove OLED 128x96

nets:
  N1: MCU1.pin_1, Grove1.VCC
  N2: MCU1.pin_3, Grove1.SDA
  N3: MCU1.pin_5, Grove1.SCL
  N4: MCU1.pin_6, MCU1.pin_9, Grove1.GND

custom parts:
  Raspberry Pi Zero: The Raspberry Pi Zero is half the size of a Model A+, with twice the utility. A tiny Raspberry Pi that’s affordable enough for any project! · 1Ghz, Single-core CPU · 512MB RAM · Mini HDMI and USB On-The-Go ports · Micro USB power · HAT-compatible 40-pin header. Jan 2018: In this version schematic has been changed so the pins match the GPIO connector. I.e. the left hand pins are all the pins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
