# Fritzing sketch TCS34725_zero (saved by Fritzing 0.9.3b)

parts:
  Part2 = Adafruit TCS34725 RGB Color Sensor [part_number="Adafruit #1334"]
  MCU1 = Raspberry Pi Zero

nets:
  N1: Part2.VIN, MCU1.pin_1, MCU1.pin_17
  N2: Part2.GND, MCU1.pin_6, MCU1.pin_9
  N3: Part2.SCL, MCU1.pin_5
  N4: Part2.SDA, MCU1.pin_3

custom parts:
  Adafruit TCS34725 RGB Color Sensor: Your electronics can now see in dazzling color with this lovely color light sensor. We found the best color sensor on the market, the TCS34725, which has RGB and Clear light sensing elements. An IR blocking filter, integrated on-chip and localized to the color sensing photodiodes, minimizes the IR spectral component of the incoming light and allows color measurements to be made accurately. The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
  Raspberry Pi Zero: The Raspberry Pi Zero is half the size of a Model A+, with twice the utility. A tiny Raspberry Pi that’s affordable enough for any project! · 1Ghz, Single-core CPU · 512MB RAM · Mini HDMI and USB On-The-Go ports · Micro USB power · HAT-compatible 40-pin header. Jan 2018: In this version schematic has been changed so the pins match the GPIO connector. I.e. the left hand pins are all the pins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
