# Fritzing sketch veml6070_zero (saved by Fritzing 0.9.3b)

parts:
  パーツ1 = VEML6070 [part_number=VEML6070]
  MCU1 = Raspberry Pi Zero

nets:
  N1: パーツ1.VDD, MCU1.pin_1, MCU1.pin_17
  N2: パーツ1.GND, MCU1.pin_6, MCU1.pin_39
  N3: パーツ1.SCL, MCU1.pin_5
  N4: パーツ1.SDA, MCU1.pin_3

notes:
  SDA
  GND

custom parts:
  VEML6070: This little sensor is a great way to add UV light sensing to any microcontroller project. The VEML6070 from Vishay has a true UV A light sensor and an I2C-controlled ADC that will take readings and integrate them for you over ~60ms to 500ms.
  Raspberry Pi Zero: The Raspberry Pi Zero is half the size of a Model A+, with twice the utility. A tiny Raspberry Pi that’s affordable enough for any project! · 1Ghz, Single-core CPU · 512MB RAM · Mini HDMI and USB On-The-Go ports · Micro USB power · HAT-compatible 40-pin header. Jan 2018: In this version schematic has been changed so the pins match the GPIO connector. I.e. the left hand pins are all the pins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
