# Fritzing sketch AS3935 Sketch (saved by Fritzing 0.9.3b)
breadboards: 1

parts:
  U1 = AS3935 Breakout [chip_label=AS3935 package="SIP (Single Inline) [THT]"]
  MCU1 = Raspberry Pi Zero

nets:
  N1: U1.VDD, MCU1.pin_1, MCU1.pin_17
  N2: U1.GND, MCU1.pin_6, MCU1.pin_39
  N3: U1.IRQ, MCU1.pin_29
  N4: U1.SCL, MCU1.pin_5
  N5: U1.SDA, MCU1.pin_3

custom parts:
  AS3935 Breakout: Franklin Lightning Sensor AS3935 Module
