# Fritzing sketch PiZero_gpio1 (saved by Fritzing 0.9.3b)
breadboards: 1

parts:
  MCU1 = Raspberry Pi Zero
  S1 = Pushbutton [package=THT]

nets:
  N1: MCU1.pin_29, S1.leg0
  N2: MCU1.pin_34, S1.leg1

custom parts:
  Pushbutton: A generic pushbutton.
