# Fritzing sketch PiZero_gpio0Motor (saved by Fritzing 0.9.3b)
breadboards: 1

parts:
  R1 = Resistor [tolerance=±5% resistance=10k package="0603 [SMD]"]
  R2 = Resistor [tolerance=±5% resistance=1k package="0603 [SMD]"]
  Q1 = Basic FET N-Channel [package="TO220 [THT]"]
  ギヤードモータ = CHIBI Geared Motor [package="SIP (Single Inline) [THT]"]
  MCU3 = Raspberry Pi Zero

nets:
  N1: R1.Pin_0, Q1.source, MCU3.pin_9, MCU3.pin_34
  N2: R1.Pin_1, R2.Pin_0, Q1.gate
  N3: R2.Pin_1, MCU3.pin_37, MCU3.pin_40
  N4: Q1.drain, ギヤードモータ.pin2
  N5: ギヤードモータ.pin1, MCU3.pin_2

notes:
  +
  -
  茶黒橙金
  茶黒赤金

custom parts:
  CHIBI Geared Motor: Micro Geared Motor
