# Fritzing sketch PiZero_gpio0MotorB_2 (saved by Fritzing 0.9.3b)
breadboards: 1

parts:
  JACK1 = 2.1mm Barrel Jack with Terminal Block
  MCU1 = Raspberry Pi Zero
  R3 = Resistor [tolerance=±5% resistance=1k package="0603 [SMD]"]
  R4 = Resistor [tolerance=±5% resistance=10k package="0603 [SMD]"]
  Q2 = Basic FET N-Channel [package="TO220 [THT]"]
  ギヤードモータ = GearedMotor [package=Motor]

nets:
  N1: JACK1.POS, ギヤードモータ.pin1
  N2: JACK1.NEG, MCU1.pin_9, MCU1.pin_34, R4.Pin_0, Q2.source
  N3: MCU1.pin_37, R3.Pin_1
  N4: R3.Pin_0, R4.Pin_1, Q2.gate
  N5: Q2.drain, ギヤードモータ.pin2

notes:
  DC 5V MOTOR POWER
  茶黒赤金
  茶黒橙金
  -
  +

custom parts:
  GearedMotor: Micro Geared Motor
