# Fritzing sketch HTU21D (saved by Fritzing 0.9.3b)
breadboards: 1

parts:
  MCU2 = Raspberry Pi Zero
  パーツ1 = HTU21D Breakout

nets:
  N1: MCU2.pin_1, MCU2.pin_17, パーツ1.3.3V
  N2: MCU2.pin_3, パーツ1.SDA
  N3: MCU2.pin_5, パーツ1.SCL
  N4: MCU2.pin_6, パーツ1.GND

custom parts:
  HTU21D Breakout: This is a breadboard friendly breakout board for the Measurement Specialties high-precision, low-power digital humidity sensor.
