# Fritzing sketch SHT30_LED (saved by Fritzing 0.9.3b)
breadboards: 1

parts:
  U2 = SHT30 breakout [package="SIP (Single Inline) [THT]"]
  MCU1 = Raspberry Pi Zero
  LED1 = LED - 5mm [color="Red (633nm)" package="5 mm [THT]"]
  R1 = Resistor [tolerance=±5% resistance=1k part_number="茶黒赤金　　" package="0603 [SMD]"]

nets:
  N1: U2.pin1, MCU1.pin_1
  N2: U2.pin2, MCU1.pin_6, MCU1.pin_9, LED1.cathode
  N3: U2.pin3, MCU1.pin_5
  N4: U2.pin4, MCU1.pin_3
  N5: MCU1.pin_37, R1.Pin_1
  N6: LED1.anode, R1.Pin_0

notes:
  LED足の長いほう

custom parts:
  SHT30 breakout: SHT30 Temperature Humidity sensor
