# Fritzing sketch TSL2591 Sketch (saved by Fritzing 0.9.3b)
breadboards: 1

parts:
  MCU1 = Raspberry Pi Zero
  パーツ1 = Adafruit TSL2591 High Dynamic Range Digital Light Sensor [part_number="Adafruit #1980"]

nets:
  N1: MCU1.pin_1, MCU1.pin_17, MCU1.pin_33, パーツ1.VCC
  N2: MCU1.pin_3, パーツ1.SDA
  N3: MCU1.pin_5, パーツ1.SCL
  N4: MCU1.pin_6, MCU1.pin_20, MCU1.pin_25, MCU1.pin_30, MCU1.pin_39, パーツ1.GND

custom parts:
  Adafruit TSL2591 High Dynamic Range Digital Light Sensor: When the future is dazzlingly-bright, this ultra-high-range luminosity sensor will help you measure it. The TSL2591 luminosity sensor is an advanced digital light sensor, ideal for use in a wide range of light situations. Compared to low cost CdS cells, this sensor is more precise, allowing for exact lux calculations and can be configured for different gain/timing ranges to detect light ranges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
