# Fritzing sketch AHT10 (saved by Fritzing 0.9.3b)
breadboards: 1

parts:
  MCU1 = Raspberry Pi Zero
  U3 = AHT10 [chip_label=AHT10 package="SIP (Single Inline) [THT]"]

nets:
  N1: MCU1.pin_1, U3.VIN
  N2: MCU1.pin_3, U3.SDA
  N3: MCU1.pin_5, U3.SCL
  N4: MCU1.pin_6, U3.GND

custom parts:
  AHT10: AHT10 I2C Temperature and Humidity Sensor Module
