# Fritzing sketch AHT20 (saved by Fritzing 0.9.3b)
breadboards: 1

parts:
  MCU1 = Raspberry Pi Zero
  パーツ2 = Adafruit AHT20 Temperature and Humidity Sensor [part_number="Adafruit #4566"]

nets:
  N1: MCU1.pin_1, MCU1.pin_17, パーツ2.VCC
  N2: MCU1.pin_3, パーツ2.SDA
  N3: MCU1.pin_5, パーツ2.SCL
  N4: MCU1.pin_6, MCU1.pin_34, パーツ2.GND

custom parts:
  Adafruit AHT20 Temperature and Humidity Sensor: The AHT20 is a nice but inexpensive temperature and humidity sensor from the same folks that brought us the DHT22. You can take sensor readings as often as you like, and it uses standard I2C so its super easy to use with any Arduino or Linux/Raspberry Pi board. This sensor has a typical accuracy of +- 2% relative humidity, and +-0.3 °C. There is only one I2C address so its not a good option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
