# Fritzing sketch AS7341 (saved by Fritzing 0.9.5d)

parts:
  パーツ1 = Adafruit AS7341
  MCU1 = Raspberry Pi Zero

nets:
  N1: パーツ1.VCC, MCU1.pin_1
  N2: パーツ1.GND, MCU1.pin_6, MCU1.pin_9
  N3: パーツ1.SCL, MCU1.pin_5
  N4: パーツ1.SDA, MCU1.pin_3
