# Fritzing sketch BH1750_zero (saved by Fritzing 0.9.3b)

parts:
  パーツ3 = BH1750
  MCU1 = Raspberry Pi Zero

nets:
  N1: パーツ3.VCC, MCU1.pin_1, MCU1.pin_17
  N2: パーツ3.GND, MCU1.pin_6, MCU1.pin_25
  N3: パーツ3.SCL, MCU1.pin_5
  N4: パーツ3.SDA, MCU1.pin_3

custom parts:
  BH1750: Light Sensor
  Raspberry Pi Zero: The Raspberry Pi Zero is half the size of a Model A+, with twice the utility. A tiny Raspberry Pi that’s affordable enough for any project! · 1Ghz, Single-core CPU · 512MB RAM · Mini HDMI and USB On-The-Go ports · Micro USB power · HAT-compatible 40-pin header. Jan 2018: In this version schematic has been changed so the pins match the GPIO connector. I.e. the left hand pins are all the pins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
