# Fritzing sketch BMP180_zero (saved by Fritzing 0.9.3b)

parts:
  パーツ2 = Barometric Pressure Sensor - BMP180 Breakout (GY-68)
  MCU1 = Raspberry Pi Zero

nets:
  N1: パーツ2.VCC, MCU1.pin_1, MCU1.pin_17
  N2: パーツ2.GND, MCU1.pin_6, MCU1.pin_25
  N3: パーツ2.SCL, MCU1.pin_5
  N4: パーツ2.SDA, MCU1.pin_3

notes:
  GND
  SCL
  SDA
  VCC

custom parts:
  Barometric Pressure Sensor - BMP180 Breakout (GY-68): This is a simple breakout board for the BMP180, a high-precision, low-power barometric pressure sensor made by Bosch Sensortec. The range of measurement is from 300hPa to 1100hPa. The sensor can be supplied with voltage ranging from 1.8V to 3.6V. Operating temperature range is -40 to +85 °C. This particular breakout board (or perhaps the configuration) is produced by Shenzhen Keep Power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
  Raspberry Pi Zero: The Raspberry Pi Zero is half the size of a Model A+, with twice the utility. A tiny Raspberry Pi that’s affordable enough for any project! · 1Ghz, Single-core CPU · 512MB RAM · Mini HDMI and USB On-The-Go ports · Micro USB power · HAT-compatible 40-pin header. Jan 2018: In this version schematic has been changed so the pins match the GPIO connector. I.e. the left hand pins are all the pins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
