# Fritzing sketch DFPlayer sketch (saved by Fritzing 0.9.3b)
breadboards: 1

parts:
  SP1 = SPEAKER [package=pcb_mount_speaker]
  Q1（1曲目再生） = MOSFET-NCHANNEL [part_number=2SK4017 package=to220v]
  Q2（再生中断・再開） = MOSFET-NCHANNEL [part_number=2SK4017 package=to220v]
  S1 = Pushbutton [package=THT]
  S2 = Pushbutton [package=THT]
  part = Resistor [tolerance=±5% resistance=33k package=THT]
  part_2 = Resistor [tolerance=±5% resistance=1k package=THT]
  part_3 = Resistor [tolerance=±5% resistance=1k package=THT]
  DFRobot_DFPlayer_Mini1 = DFRobot DFPlayer Mini [part_number=DFR0299]
  MCU1 = Raspberry Pi Zero

nets:
  N1: SP1.+, DFRobot_DFPlayer_Mini1.SPK_2
  N2: SP1.-, DFRobot_DFPlayer_Mini1.SPK_1
  N3: Q1（1曲目再生）.G, part_2.Pin_1
  N4: Q1（1曲目再生）.D, part.Pin_1, DFRobot_DFPlayer_Mini1.ADKEY_1
  N5: Q1（1曲目再生）.S, Q2（再生中断・再開）.S, S1.leg1, S2.leg1, DFRobot_DFPlayer_Mini1.GND-1, DFRobot_DFPlayer_Mini1.GND-2, MCU1.pin_39
  N6: Q2（再生中断・再開）.G, part_3.Pin_1
  N7: Q2（再生中断・再開）.D, part.Pin_0
  N8: S1.leg0, DFRobot_DFPlayer_Mini1.IO_1
  N9: S2.leg0, DFRobot_DFPlayer_Mini1.IO_2
  N10: part_2.Pin_0, MCU1.pin_37
  N11: part_3.Pin_0, MCU1.pin_35
  N12: DFRobot_DFPlayer_Mini1.VCC, MCU1.pin_2, MCU1.pin_4

notes:
  S1: 前の曲再生／長押し音量下げる
  S2: 次の曲再生／長押し音量上げる
  G　D　S

custom parts:
  DFRobot DFPlayer Mini: The DFPlayer Mini is a small and low cost MP3 module with an simplified output directly to the speaker. The module can be used as a stand alone module with attached battery, speaker and push buttons or used in combination with an Arduino UNO or any other with RX/TX capabilities.
