# Fritzing sketch DRV2605L (saved by Fritzing 0.9.5d)

parts:
  パーツ1 = Adafruit DRV2605L [part_number="Adafruit #2305"]
  MCU1 = Raspberry Pi Zero

nets:
  N1: パーツ1.VIN, MCU1.pin_1, MCU1.pin_17
  N2: パーツ1.GND, MCU1.pin_6, MCU1.pin_39
  N3: パーツ1.SCL, MCU1.pin_5
  N4: パーツ1.SDA, MCU1.pin_3

custom parts:
  Adafruit DRV2605L: The DRV2605 from TI is a fancy little motor driver. Rather than controlling a stepper motor or DC motor, its designed specifically for controlling haptic motors - buzzers and vibration motors. Normally one would just turn those kinds of motors on and off, but this driver has the ability to have various effects when driving a vibe motor. For example, ramping the vibration level up and down,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
