# Fritzing sketch PiZero_gpio-inoutMotor (saved by Fritzing 0.9.3b)
breadboards: 1

parts:
  R2 = Resistor [tolerance=±5% resistance=1k package="0603 [SMD]"]
  Q1 = Basic FET N-Channel [package="TO220 [THT]"]
  ギヤードモータ = CHIBI Geared Motor [package="SIP (Single Inline) [THT]"]
  MCU3 = Raspberry Pi Zero
  R1 = Resistor [tolerance=±5% resistance=10k package="0603 [SMD]"]
  S1 = Pushbutton [package=THT]

nets:
  N1: R2.Pin_0, Q1.gate, R1.Pin_1
  N2: R2.Pin_1, MCU3.pin_37, MCU3.pin_40
  N3: Q1.drain, ギヤードモータ.pin2
  N4: Q1.source, MCU3.pin_9, MCU3.pin_34, R1.Pin_0, S1.leg0
  N5: ギヤードモータ.pin1, MCU3.pin_2
  N6: MCU3.pin_29, S1.leg1

notes:
  +
  -
  茶黒橙金
  茶黒赤金

custom parts:
  CHIBI Geared Motor: Micro Geared Motor
  Pushbutton: A generic pushbutton.
