# Fritzing sketch PiZero_gpio_TTP223 (saved by Fritzing 0.9.3b)
breadboards: 1

parts:
  U2 = TTP223touch [chip_label=TTP223 package="SIP (Single Inline) [THT]"]
  MCU1 = Raspberry Pi Zero

nets:
  N1: U2.VCC, MCU1.pin_1
  N2: U2.I/O, MCU1.pin_29
  N3: U2.GND, MCU1.pin_6, MCU1.pin_34

custom parts:
  TTP223touch: TTP223 touch sensor
