# Fritzing sketch HBridge_L298N (saved by Fritzing 0.9.3b)

parts:
  S1 = H-Bridge with L298N
  M1 = DC Motor
  MCU2 = Raspberry Pi Zero

nets:
  12V: S1.12V, S1.5V, MCU2.pin_2
  N1: S1.GND, MCU2.pin_6
  N2: S1.ENA, S1.ENA-5V
  N3: S1.IN1, MCU2.pin_38
  N4: S1.IN2, MCU2.pin_40
  N5: S1.M1-01, M1.pin_2
  N6: S1.M1-02, M1.pin_1

notes:
  5V DC Motor

custom parts:
  H-Bridge with L298N: h-bridge
