# Fritzing sketch PiZero_gpio0Motor_2 (saved by Fritzing 0.9.3b)
breadboards: 1

parts:
  R2 = Resistor [tolerance=±5% resistance=1k package="0603 [SMD]"]
  Q1 = Basic FET N-Channel [package="TO220 [THT]"]
  R1 = Resistor [tolerance=±5% resistance=10k package="0603 [SMD]"]
  MCU3 = Raspberry Pi Zero
  ギヤードモータ = GearedMotor [package=Motor]

nets:
  N1: R2.Pin_0, Q1.gate, R1.Pin_1
  N2: R2.Pin_1, MCU3.pin_37
  N3: Q1.drain, ギヤードモータ.pin2
  N4: Q1.source, R1.Pin_0, MCU3.pin_9, MCU3.pin_34
  N5: MCU3.pin_2, MCU3.pin_4, ギヤードモータ.pin1

notes:
  +
  -
  茶黒橙金
  茶黒赤金

custom parts:
  GearedMotor: Micro Geared Motor
