# Fritzing sketch i2c1602LCD (saved by Fritzing 0.9.3b)

parts:
  MCU1 = Raspberry Pi Zero
  パーツ1 = LCD1602-I2C

nets:
  N1: MCU1.pin_2, パーツ1.VCC
  N2: MCU1.pin_3, パーツ1.SDA
  N3: MCU1.pin_5, パーツ1.SCL
  N4: MCU1.pin_6, パーツ1.GND

notes:
  NOTE3:　LCDのポテンショメータの調節が必要です
  NOTE2:　VCCには5Vを接続しないとLCDのコントラストが低くなります
  NOTE1:　バックライトLEDジャンパーは接続してください

custom parts:
  Raspberry Pi Zero: The Raspberry Pi Zero is half the size of a Model A+, with twice the utility. A tiny Raspberry Pi that’s affordable enough for any project! · 1Ghz, Single-core CPU · 512MB RAM · Mini HDMI and USB On-The-Go ports · Micro USB power · HAT-compatible 40-pin header. Jan 2018: In this version schematic has been changed so the pins match the GPIO connector. I.e. the left hand pins are all the pins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
  LCD1602-I2C: A standard character display, usually with 2x16 characters. Comes in many colors with LCM1602 IIC attached.
