# Fritzing sketch ICM20948 Sketch (saved by Fritzing 0.9.3b)
breadboards: 1

parts:
  MCU1 = Raspberry Pi Zero
  パーツ1 = Adafruit ICM20948

nets:
  N1: MCU1.pin_1, MCU1.pin_17, MCU1.pin_33, パーツ1.VIN
  N2: MCU1.pin_3, パーツ1.SDI/SDA
  N3: MCU1.pin_5, パーツ1.SCK/SCL
  N4: MCU1.pin_6, MCU1.pin_20, MCU1.pin_25, MCU1.pin_30, MCU1.pin_39, パーツ1.GND
