# Fritzing sketch INA219_zero (saved by Fritzing 0.9.3b)

parts:
  パーツ1 = INA219 High Side DC Current Sensor Breakout [part_number=904]
  M1 = CHIBI Geared Motor [package="SIP (Single Inline) [THT]"]
  VCC1 = Battery
  MCU1 = Raspberry Pi Zero

nets:
  N1: パーツ1.VIN-, M1.pin2
  N2: パーツ1.VIN+, VCC1.+
  N3: パーツ1.VCC, MCU1.pin_1, MCU1.pin_17
  N4: パーツ1.GND, M1.pin1, VCC1.-, MCU1.pin_6, MCU1.pin_20, MCU1.pin_34
  N5: パーツ1.SCL, MCU1.pin_5
  N6: パーツ1.SDA, MCU1.pin_3

notes:
  VCC
  GND
  SCL
  SDA
  Vin-
  Vin+

custom parts:
  INA219 High Side DC Current Sensor Breakout: This breakout board will solve all your power-monitoring problems. Instead of struggling with two multimeters, you can just use the handy INA219B chip on this breakout to both measure both the high side voltage and DC current draw over I2C with 1% precision. Most current-measuring devices such as our current panel meter are only good for low side measuring. That means that unless you want to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
  CHIBI Geared Motor: Micro Geared Motor
  Raspberry Pi Zero: The Raspberry Pi Zero is half the size of a Model A+, with twice the utility. A tiny Raspberry Pi that’s affordable enough for any project! · 1Ghz, Single-core CPU · 512MB RAM · Mini HDMI and USB On-The-Go ports · Micro USB power · HAT-compatible 40-pin header. Jan 2018: In this version schematic has been changed so the pins match the GPIO connector. I.e. the left hand pins are all the pins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
