# Fritzing sketch LTR390 Sketch (saved by Fritzing 0.9.3b)
breadboards: 1

parts:
  MCU1 = Raspberry Pi Zero
  パーツ2 = Adafruit LTR390 UV Light Sensor [part_number="Adafruit #4831"]

nets:
  N1: MCU1.pin_1, MCU1.pin_17, MCU1.pin_33, パーツ2.VCC
  N2: MCU1.pin_3, パーツ2.SDA
  N3: MCU1.pin_5, パーツ2.SCL
  N4: MCU1.pin_6, MCU1.pin_20, MCU1.pin_25, MCU1.pin_30, MCU1.pin_39, パーツ2.GND

custom parts:
  Adafruit LTR390 UV Light Sensor: The LTR390 is one of the few low-cost UV sensors available, and it's a pretty nice one! With both ambient light and UVA sensing with a peak spectral response between 300 and 350nm. You can use it for measuring how much sun you can get before needing to covering up. Unlike the Si1145, this sensor will not give you UV Index readings. However, the Si1145 does UV Index approximations based on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
