# Fritzing sketch MCP9808 (saved by Fritzing 0.9.5d)

parts:
  Grove1 = MCP9808
  Raspberry_Pi_1 = Raspberry Pi 3 [part_number=RPI-3-V1.2]

nets:
  GND: Grove1.GND, Raspberry_Pi_1.GND
  VCC: Grove1.VCC, Raspberry_Pi_1.3v3
  N1: Grove1.SDA, Raspberry_Pi_1.GPIO2
  N2: Grove1.SCL, Raspberry_Pi_1.GPIO3

custom parts:
  MCP9808: An analog temperature sensor
