# Fritzing sketch neopixel-i2c_zero (saved by Fritzing 0.9.3b)

parts:
  NEOPIXEL1 = Neopixel 8x8 Matrix
  BRD1 = Neopixel I2C
  MCU1 = Raspberry Pi Zero

nets:
  N1: NEOPIXEL1.DIN, BRD1.DATA
  N2: NEOPIXEL1.VCC, BRD1.+5V#6
  N3: NEOPIXEL1.GND, BRD1.GND#8
  N4: BRD1.+3.3V, MCU1.pin_1, MCU1.pin_17
  N5: BRD1.SDA, MCU1.pin_3
  N6: BRD1.SCL, MCU1.pin_5
  N7: BRD1.GND#3, MCU1.pin_6, MCU1.pin_39
  N8: BRD1.+5V#4, MCU1.pin_2, MCU1.pin_4

notes:
  GND
  D-IN
  VCC

custom parts:
  Neopixel 8x8 Matrix: Adafruit Neopixel 8x8 Matrix
  Neopixel I2C: neopixel i2c driver board
  Raspberry Pi Zero: The Raspberry Pi Zero is half the size of a Model A+, with twice the utility. A tiny Raspberry Pi that’s affordable enough for any project! · 1Ghz, Single-core CPU · 512MB RAM · Mini HDMI and USB On-The-Go ports · Micro USB power · HAT-compatible 40-pin header. Jan 2018: In this version schematic has been changed so the pins match the GPIO connector. I.e. the left hand pins are all the pins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
