# Fritzing sketch pca9685_zero (saved by Fritzing 0.9.3b)

parts:
  PCA9685_PWM = PCA9685 16x12-bit PWM Breakout
  MICRO_SERVO = Tower Pro SG90 servo [part_number=101246]
  MOTOR_Power_5V = 2.1mm Barrel Jack with Terminal Block
  MCU1 = Raspberry Pi Zero

nets:
  N1: PCA9685_PWM.no_name_yet#0, MICRO_SERVO.Signal
  N2: PCA9685_PWM.no_name_yet#100, PCA9685_PWM.no_name_yet#706, MICRO_SERVO.+5V, MOTOR_Power_5V.POS
  N3: PCA9685_PWM.no_name_yet#601, PCA9685_PWM.no_name_yet#701, PCA9685_PWM.no_name_yet#1000, MICRO_SERVO.GND, MOTOR_Power_5V.NEG, MCU1.pin_6
  N4: PCA9685_PWM.no_name_yet#603, MCU1.pin_5
  N5: PCA9685_PWM.no_name_yet#604, MCU1.pin_3
  N6: PCA9685_PWM.no_name_yet#605, MCU1.pin_1

notes:
  SCL
  SDA
  GND
  3V/VDD

custom parts:
  Tower Pro SG90 servo: Original file by John De Cristofaro http://www.adafruit.com/products/1449 Adafruit Feedback Servo (Small) Edited by: e-radionica.com 28/9/2015
  Raspberry Pi Zero: The Raspberry Pi Zero is half the size of a Model A+, with twice the utility. A tiny Raspberry Pi that’s affordable enough for any project! · 1Ghz, Single-core CPU · 512MB RAM · Mini HDMI and USB On-The-Go ports · Micro USB power · HAT-compatible 40-pin header. Jan 2018: In this version schematic has been changed so the pins match the GPIO connector. I.e. the left hand pins are all the pins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
