# Fritzing sketch SGP30 (saved by Fritzing 0.9.5)

parts:
  SENSOR = M5Stack Mini Unit TVOC/eCO2 (SGP30) [package=THT]
  MCU1 = Raspberry Pi Zero

nets:
  N1: SENSOR.GND, MCU1.pin_6
  N2: SENSOR.VCC, MCU1.pin_1
  N3: SENSOR.SDA, MCU1.pin_3
  N4: SENSOR.SCL, MCU1.pin_5

custom parts:
  M5Stack Mini Unit TVOC/eCO2 (SGP30): M5Stack Mini Unit TVOC/eCO2 (SKU U088). Sensirion SGP30 gas sensor in a 24 x 24 x 8 mm plastic unit with a HY2.0-4P (Grove) I2C socket. I2C address 0x58. Labelled 5 V, but the board carries an RT9193-1.8V LDO and a BSS138 bidirectional level shifter whose high-side pull-ups tie to the connector VCC pin, so drive VCC at 3.3 V when connecting to a Raspberry Pi. Feeding 5 V would put 5 V on the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
