# Fritzing sketch SGP40 Sketch (saved by Fritzing 0.9.3b)
breadboards: 1

parts:
  MCU1 = Raspberry Pi Zero
  パーツ4 = Adafruit SGP40

nets:
  N1: MCU1.pin_1, MCU1.pin_17, MCU1.pin_33, パーツ4.VCC
  N2: MCU1.pin_3, パーツ4.SDA
  N3: MCU1.pin_5, パーツ4.SCL
  N4: MCU1.pin_6, MCU1.pin_14, MCU1.pin_20, MCU1.pin_25, MCU1.pin_30, MCU1.pin_39, パーツ4.GND
