# Fritzing sketch SHT30_MOTORA (saved by Fritzing 0.9.3b)
breadboards: 1

parts:
  R2 = Resistor [tolerance=±5% resistance=1k package="0603 [SMD]"]
  Q1 = Basic FET N-Channel [package="TO220 [THT]"]
  ギヤードモータ = CHIBI Geared Motor [package="SIP (Single Inline) [THT]"]
  R1 = Resistor [tolerance=±5% resistance=10k package="0603 [SMD]"]
  MCU2 = Raspberry Pi Zero
  U1 = SHT30 breakout [package="SIP (Single Inline) [THT]"]

nets:
  N1: R2.Pin_0, Q1.gate, R1.Pin_1
  N2: R2.Pin_1, MCU2.pin_37
  N3: Q1.drain, ギヤードモータ.pin2
  N4: Q1.source, R1.Pin_0, MCU2.pin_9, MCU2.pin_34, MCU2.pin_39, U1.pin2
  N5: ギヤードモータ.pin1, MCU2.pin_2
  N6: MCU2.pin_1, MCU2.pin_17, U1.pin1
  N7: MCU2.pin_3, U1.pin4
  N8: MCU2.pin_5, U1.pin3

notes:
  +
  -
  茶黒橙金
  茶黒赤金
  5V
  3.3V

custom parts:
  CHIBI Geared Motor: Micro Geared Motor
  SHT30 breakout: SHT30 Temperature Humidity sensor
