# Fritzing sketch SHT40 (saved by Fritzing 0.9.3b)
breadboards: 1

parts:
  U3 = SHT30 breakout [package="SIP (Single Inline) [THT]"]
  MCU1 = Raspberry Pi Zero

nets:
  N1: U3.pin1, MCU1.pin_1
  N2: U3.pin2, MCU1.pin_6, MCU1.pin_9
  N3: U3.pin3, MCU1.pin_5
  N4: U3.pin4, MCU1.pin_3

custom parts:
  SHT30 breakout: SHT30 Temperature Humidity sensor
  Raspberry Pi Zero: The Raspberry Pi Zero is half the size of a Model A+, with twice the utility. A tiny Raspberry Pi that’s affordable enough for any project! · 1Ghz, Single-core CPU · 512MB RAM · Mini HDMI and USB On-The-Go ports · Micro USB power · HAT-compatible 40-pin header. Jan 2018: In this version schematic has been changed so the pins match the GPIO connector. I.e. the left hand pins are all the pins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
