# Fritzing sketch SSD1306_zero (saved by Fritzing 0.9.3b)

parts:
  o1 = Module display OLED I2C 128x64 SSD1306 [package=THT]
  MCU1 = Raspberry Pi Zero

nets:
  N1: o1.GND, MCU1.pin_6
  N2: o1.VCC, MCU1.pin_1
  N3: o1.SCL, MCU1.pin_5
  N4: o1.SDA, MCU1.pin_3

custom parts:
  Module display OLED I2C 128x64 SSD1306: Ecran OLED I2C SSD163 de 128x64 avec connexion I2C
  Raspberry Pi Zero: The Raspberry Pi Zero is half the size of a Model A+, with twice the utility. A tiny Raspberry Pi that’s affordable enough for any project! · 1Ghz, Single-core CPU · 512MB RAM · Mini HDMI and USB On-The-Go ports · Micro USB power · HAT-compatible 40-pin header. Jan 2018: In this version schematic has been changed so the pins match the GPIO connector. I.e. the left hand pins are all the pins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
