# Fritzing sketch TMP117 (saved by Fritzing 0.9.5d)

parts:
  SparkFun_High_Precision_Temperature_Sensor_-_TMP117_(Qwiic)1 = SparkFun High Precision Temperature Sensor - TMP117 (Qwiic) [part_number=SEN-15805]
  MCU1 = Raspberry Pi Zero

nets:
  N1: SparkFun_High_Precision_Temperature_Sensor_-_TMP117_(Qwiic)1.GND, MCU1.pin_6, MCU1.pin_25
  N2: SparkFun_High_Precision_Temperature_Sensor_-_TMP117_(Qwiic)1.3.3V, MCU1.pin_1
  N3: SparkFun_High_Precision_Temperature_Sensor_-_TMP117_(Qwiic)1.SDA, MCU1.pin_3
  N4: SparkFun_High_Precision_Temperature_Sensor_-_TMP117_(Qwiic)1.SCL, MCU1.pin_5

custom parts:
  SparkFun High Precision Temperature Sensor - TMP117 (Qwiic): The SparkFun Qwiic TMP117 breakout is a high precision temperature sensor equipped with an I2C interface. It outputs temperature readings with high precision of ±0.1°C across the temperature range of -20°C to +50°Cs with no calibration and a maximum range from -55°C to 150°C. The SparkFun High Precision Temperature Sensor also has a very low power consumption rate which minimizes the impact of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
