# Fritzing sketch VL53L0X_zero (saved by Fritzing 0.9.3b)

parts:
  パーツ4 = Adafruit VL53L0X Time of Flight Distance Sensor [part_number="Adafruit #3317"]
  MCU1 = Raspberry Pi Zero

nets:
  N1: パーツ4.VIN, MCU1.pin_1
  N2: パーツ4.GND, MCU1.pin_6
  N3: パーツ4.SCL, MCU1.pin_5
  N4: パーツ4.SDA, MCU1.pin_3

notes:
  VCC
  GND
  SCL
  SDA

custom parts:
  Adafruit VL53L0X Time of Flight Distance Sensor: The VL53L0X is a Time of Flight distance sensor like no other you've used! The sensor contains a very tiny invisible laser source, and a matching sensor. The VL53L0X can detect the "time of flight", or how long the light has taken to bounce back to the sensor. Since it uses a very narrow light source, it is good for determining distance of only the surface directly in front of it. Unlike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
  Raspberry Pi Zero: The Raspberry Pi Zero is half the size of a Model A+, with twice the utility. A tiny Raspberry Pi that’s affordable enough for any project! · 1Ghz, Single-core CPU · 512MB RAM · Mini HDMI and USB On-The-Go ports · Micro USB power · HAT-compatible 40-pin header. Jan 2018: In this version schematic has been changed so the pins match the GPIO connector. I.e. the left hand pins are all the pins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
