# Fritzing sketch RFID2_WS1850S (saved by Fritzing 0.9.3b)

parts:
  MCU1 = Raspberry Pi Zero
  U1 = RFID2_WS1850S [package="SIP (Single Inline) [THT]"]

nets:
  N1: MCU1.pin_2, MCU1.pin_4, U1.pin3
  N2: MCU1.pin_3, U1.pin2
  N3: MCU1.pin_5, U1.pin1
  N4: MCU1.pin_6, U1.pin4

custom parts:
  Raspberry Pi Zero: The Raspberry Pi Zero is half the size of a Model A+, with twice the utility. A tiny Raspberry Pi that’s affordable enough for any project! · 1Ghz, Single-core CPU · 512MB RAM · Mini HDMI and USB On-The-Go ports · Micro USB power · HAT-compatible 40-pin header. Jan 2018: In this version schematic has been changed so the pins match the GPIO connector. I.e. the left hand pins are all the pins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
  RFID2_WS1850S: m5 RFID2 I2C RFID Reader/Writer WG1850S compatible with RC522
