# Fritzing sketch s (saved by Fritzing 0.9.3b)
breadboards: 1

parts:
  Raspberry_Pi_1 = Raspberry Pi 3 [part_number=RPI-3-V1.2]
  S2 = Pushbutton [package="[THT]"]
  LED1 = smd LED [color="Red (633nm)" package="0805 [SMD]"]
  part = Resistor [tolerance=±5% resistance=220 package="0603 [SMD]"]

nets:
  N1: Raspberry_Pi_1.GPIO5, S2.Pin_1, S2.Pin_2
  N2: Raspberry_Pi_1.GPIO26, LED1.anode
  N3: Raspberry_Pi_1.GND, S2.Pin_3, S2.Pin_4, part.Pin_0
  N4: LED1.cathode, part.Pin_1

notes:
  -
  赤赤茶金
