# Fritzing sketch schematic (saved by Fritzing 0.9.3b)
breadboards: 1

parts:
  Raspberry_Pi_1 = Raspberry Pi 3 [part_number=RPI-3-V1.2]
  I2C_1 = ADT7410 AKIZUKI [part_number=ADT7410 package="SIP (Single Inline) [THT]"]
  Q1 = Basic FET N-Channel [package="TO220 [THT]"]
  R1 = Resistor [tolerance=±5% resistance=1k package="0603 [SMD]"]
  R2 = Resistor [tolerance=±5% resistance=10k package=THT]
  M1 = CHIBI Geared Motor [part_number="ギヤードモータ　" package="SIP (Single Inline) [THT]"]

nets:
  N1: Raspberry_Pi_1.3v3, I2C_1.pin4
  N2: Raspberry_Pi_1.GPIO2, I2C_1.pin2
  N3: Raspberry_Pi_1.GPIO3, I2C_1.pin3
  N4: Raspberry_Pi_1.GND, I2C_1.pin1, Q1.source, R2.Pin_0
  N5: Raspberry_Pi_1.GPIO26, R1.Pin_0
  N6: Raspberry_Pi_1.5V, M1.pin1
  N7: Q1.gate, R1.Pin_1, R2.Pin_1
  N8: Q1.drain, M1.pin2

custom parts:
  ADT7410 AKIZUKI: ADT7410 I2C breakout AKIZUKI ver
  CHIBI Geared Motor: Micro Geared Motor
