# Fritzing sketch schematic_sht (saved by Fritzing 0.9.3b)
breadboards: 1

parts:
  Raspberry_Pi_1 = Raspberry Pi 3 [part_number=RPI-3-V1.2]
  Q1 = Basic FET N-Channel [package="TO220 [THT]"]
  R1 = Resistor [tolerance=±5% resistance=1k package="0603 [SMD]"]
  R2 = Resistor [tolerance=±5% resistance=10k package=THT]
  M1 = CHIBI Geared Motor [part_number="ギヤードモータ　" package="SIP (Single Inline) [THT]"]
  U1 = SHT30 breakout [part_number=SHT30 package="SIP (Single Inline) [THT]"]

nets:
  N1: Raspberry_Pi_1.3v3, U1.pin1
  N2: Raspberry_Pi_1.GPIO2, U1.pin4
  N3: Raspberry_Pi_1.GPIO3, U1.pin3
  N4: Raspberry_Pi_1.GND, Q1.source, R2.Pin_0, U1.pin2
  N5: Raspberry_Pi_1.GPIO26, R1.Pin_0
  N6: Raspberry_Pi_1.5V, M1.pin1
  N7: Q1.gate, R1.Pin_1, R2.Pin_1
  N8: Q1.drain, M1.pin2

custom parts:
  CHIBI Geared Motor: Micro Geared Motor
  SHT30 breakout: SHT30 Temperature Humidity sensor
