# Fritzing sketch DC3motor (saved by Fritzing 0.9.3b)
breadboards: 1

parts:
  Raspberry_Pi_1 = Raspberry Pi 3 [part_number=RPI-3-V1.2]
  R1 = Resistor [tolerance=±5% resistance=10k package="0603 [SMD]"]
  R2 = Resistor [tolerance=±5% resistance=1k package="0603 [SMD]"]
  Q1 = Basic FET N-Channel [package="TO220 [THT]"]
  S1 = Momentary Switch [package=ksa_sealed_tac_switch]
  ギヤードモータ = CHIBI Geared Motor [package="SIP (Single Inline) [THT]"]

nets:
  N1: Raspberry_Pi_1.GPIO5, Raspberry_Pi_1.GPIO6, S1.4
  N2: Raspberry_Pi_1.GPIO26, R2.Pin_1
  N3: Raspberry_Pi_1.GND, R1.Pin_0, Q1.source, S1.1
  N4: Raspberry_Pi_1.5V, ギヤードモータ.pin1
  N5: R1.Pin_1, R2.Pin_0, Q1.gate
  N6: Q1.drain, ギヤードモータ.pin2

notes:
  +
  -
  茶黒橙金
  茶黒赤金
  Note: 抵抗値の読み方は０章のリンクを参照

custom parts:
  CHIBI Geared Motor: Micro Geared Motor
