# Fritzing sketch schematic_S2 (saved by Fritzing 0.9.3b)

parts:
  Raspberry_Pi_1 = Raspberry Pi 3 [part_number=RPI-3-V1.2]
  I2C_1 = ADT7410 AKIZUKI [part_number=ADT7410 package="SIP (Single Inline) [THT]"]

nets:
  N1: Raspberry_Pi_1.3v3, I2C_1.pin4
  N2: Raspberry_Pi_1.GPIO2, I2C_1.pin2
  N3: Raspberry_Pi_1.GPIO3, I2C_1.pin3
  N4: Raspberry_Pi_1.GND, I2C_1.pin1

custom parts:
  ADT7410 AKIZUKI: ADT7410 I2C breakout AKIZUKI ver
