# Fritzing sketch adt7410 (saved by Fritzing 0.9.3b)
breadboards: 1

parts:
  LED1 = LED - 5mm [color="Blue (505nm)" package="5 mm [THT]"]
  R1 = Resistor [tolerance=±5% resistance=100 package="1206 [SMD]"]
  R3 = Resistor [tolerance=±5% resistance=10k package="0603 [SMD]"]
  R2 = Resistor [tolerance=±5% resistance=10k package="0603 [SMD]"]
  U2 = ADT7410 [part_number=ADT7410]
  U1 = TY51822r3 [package=dip32]

nets:
  N1: LED1.cathode, R1.Pin_1
  N2: LED1.anode, U1.P0_21
  N3: R1.Pin_0, U1.GND#31
  N4: R3.Pin_0, U2.SDA, U1.P0_30, U1.P0_1
  VDD: R3.Pin_1, R2.Pin_1, U2.VDD, U1.VDD
  N5: R2.Pin_0, U2.SCL, U1.P0_29, U1.P0_14
  N6: U2.GND, U1.GND#6

custom parts:
  TY51822r3: SwitchScience TY51822r3
