# Fritzing sketch button (saved by Fritzing 0.9.3b)
circuit board: 8.46667cm x 5.64444cm
breadboards: 1

parts:
  LED1 = smd LED [color="Blue (505nm)" package="1206 [SMD]"]
  U1 = TY51822r3 [package=dip32]
  R2 = Resistor [tolerance=±5% resistance=330 package="0805 [SMD]"]
  R1 = Resistor [tolerance=±5% resistance=100 package="0805 [SMD]"]
  LED2 = smd LED [color="Red (635nm)" package="1206 [SMD]"]
  S1 = Pushbutton [package="[SMD]"]

nets:
  N1: LED1.cathode, R1.Pin_1
  N2: LED1.anode, U1.P0_21
  N3: U1.P0_29, U1.P0_14
  N4: U1.P0_30, U1.P0_1
  N5: U1.GND#6, R2.Pin_1, S1.Pin_3, S1.Pin_4
  N6: U1.P0_7, LED2.anode
  N7: U1.P0_5, S1.Pin_1, S1.Pin_2
  N8: U1.GND#31, R1.Pin_0
  N9: R2.Pin_0, LED2.cathode

custom parts:
  TY51822r3: SwitchScience TY51822r3
