# Fritzing sketch dcmotor (saved by Fritzing 0.9.3b)
breadboards: 1

parts:
  U1 = TY51822r3 [package=dip32]
  Q1 = Basic FET N-Channel [part_number=2SK4017 package="D2Pak [SMD]"]
  VCC1 = Battery
  R1 = Resistor [tolerance=±5% resistance=1k package=THT]
  R2 = Resistor [tolerance=±5% resistance=10k package=THT]
  LED1 = LED - 5mm [color="Blue (505nm)" package="5 mm [THT]"]
  R3 = Resistor [tolerance=±5% resistance=100 package="1206 [SMD]"]
  M1 = DC Motor
  D1 = P1000K [part_number=1N4007]
  S1 = Pushbutton [package="[SMD]"]

nets:
  N1: U1.P0_29, U1.P0_14
  N2: U1.P0_30, U1.P0_1
  N3: U1.GND#6, Q1.source, VCC1.-, R2.Pin_1, S1.Pin_3, S1.Pin_4
  N4: U1.P0_7, R1.Pin_1
  N5: U1.P0_5, S1.Pin_1, S1.Pin_2
  N6: U1.P0_21, LED1.anode
  N7: U1.GND#31, R3.Pin_0
  N8: Q1.Gate, R1.Pin_0, R2.Pin_0
  N9: Q1.drain, M1.pin_2, D1.anode
  N10: VCC1.+, M1.pin_1, D1.cathode
  N11: LED1.cathode, R3.Pin_1

custom parts:
  TY51822r3: SwitchScience TY51822r3
