# Fritzing sketch readGpio (saved by Fritzing 0.9.3b)
breadboards: 1

parts:
  U1 = TY51822r3 [package=dip32]
  LED1 = smd LED [color="Blue (505nm)" package="1206 [SMD]"]
  R1 = Resistor [tolerance=±5% resistance=100 package="0805 [SMD]"]
  S1 = Momentary Switch [package=ksa_sealed_tac_switch]

nets:
  N1: U1.P0_29, U1.P0_14
  N2: U1.P0_30, U1.P0_1
  N3: U1.GND#6, S1.4
  N4: U1.P0_5, S1.2
  N5: U1.P0_21, LED1.anode
  N6: U1.GND#31, R1.Pin_0
  N7: LED1.cathode, R1.Pin_1

custom parts:
  TY51822r3: SwitchScience TY51822r3
