# Fritzing sketch grove (saved by Fritzing 0.9.3b)
breadboards: 1

parts:
  U1 = TY51822r3 [package=dip32]
  Grove5 = Grove Digital Light Sensor
  Grove6 = Grove 3 Axis Accelerometer Sensor
  U2 = ADT7410 [part_number=ADT7410]
  Grove7 = Grove 3 Axis Accelerometer Sensor
  LED1 = LED - 5mm [color="Blue (505nm)" package="5 mm [THT]"]
  R1 = Resistor [tolerance=±5% resistance=100 package="2512 [SMD]"]
  R2 = Resistor [tolerance=±5% resistance=10k package="1206 [SMD]"]
  R3 = Resistor [tolerance=±5% resistance=10k package="1206 [SMD]"]
  U3 = GP2Y0E03 [part_number=GP2Y0E03]

nets:
  N1: U1.P0_29, U1.P0_14, Grove7.SCL1, R3.Pin_0, U3.SCL
  N2: U1.P0_30, U1.P0_1, Grove7.SDA1, R2.Pin_0, U3.SDA
  GND1: U1.GND#6, Grove7.GND1, U3.GND
  VDD: U1.VDD, Grove7.VCC1, R2.Pin_1, R3.Pin_1, U3.VDD, U3.VINIO, U3.GPIO1
  N3: U1.P0_21, LED1.anode
  N4: U1.GND#31, R1.Pin_0
  GND: Grove5.GND, Grove7.GND3
  N5: Grove5.VCC, Grove7.VCC3
  N6: Grove5.SDA, Grove7.SDA3
  N7: Grove5.SCL, Grove7.SCL3
  GND_2: Grove6.GND, Grove7.GND4
  N8: Grove6.VCC, Grove7.VCC4
  N9: Grove6.SDA, Grove7.SDA4
  N10: Grove6.SCL, Grove7.SCL4
  GND_3: U2.GND, Grove7.GND2
  N11: U2.SDA, Grove7.SDA2
  N12: U2.SCL, Grove7.SCL2
  N13: U2.VDD, Grove7.VCC2
  N14: LED1.cathode, R1.Pin_1

custom parts:
  TY51822r3: SwitchScience TY51822r3
  Grove Digital Light Sensor: An Digital Light Sensor
  Grove 3 Axis Accelerometer Sensor: I2C 3 Axis Accelerometer Sensor
  Grove 3 Axis Accelerometer Sensor: I2C 3 Axis Accelerometer Sensor
